# Fritzing sketch Untitled Sketch (saved by Fritzing 0.9.3b)
breadboards: 1

parts:
  S1 = Pushbutton [package="[THT]"]
  T1 = LM34 Temperature Sensor [package="TO92 [THT]"]
  R1 = Resistor [tolerance=±5% resistance=220 package=THT]
  Part2 = Arduino Uno (Rev3)

nets:
  N1: S1.Pin_1, S1.Pin_2, R1.Pin_0, Part2.D10_PWM/SS
  N2: S1.Pin_3, S1.Pin_4, Part2.5V
  GND: T1.+Vs, T1.GND, R1.Pin_1, Part2.GND
  N3: T1.Vout, Part2.A0
